# Fritzing sketch fritzing final2 (saved by Fritzing 0.9.3b)
breadboards: 2

parts:
  Componente2 = Arduino Uno (Rev3)
  Componente3 = Solar Cell
  R2 = Photocell (LDR) [package=THT]
  R3 = Photocell (LDR) [package=THT]
  R4 = Photocell (LDR) [package=THT]
  R9 = Resistor [tolerance=±5% resistance=10k package="0402 [SMD]"]
  R10 = Photocell (LDR) [package=THT]
  R11 = Resistor [tolerance=±5% resistance=10k package="0402 [SMD]"]
  R12 = Resistor [tolerance=±5% resistance=10k package="0402 [SMD]"]
  R13 = Resistor [tolerance=±5% resistance=10k package="0402 [SMD]"]
  VM1 = Voltmeter (3 wire)
  J1 = Basic Servo
  J2 = Basic Servo

nets:
  N1: Componente2.A0, R9.Pin_1, R10.pin_1
  N2: Componente2.A1, R2.pin_1, R11.Pin_1
  N3: Componente2.A2, R3.pin_1, R12.Pin_1
  N4: Componente2.A3, R4.pin_1, R13.Pin_1
  N5: Componente2.D9_PWM, J1.pulse
  N6: Componente2.D10_PWM/SS, J2.pulse
  VCC: Componente2.5V, J1.vcc, J2.vcc
  GND: Componente2.GND, R9.Pin_0, R11.Pin_0, R12.Pin_0, R13.Pin_0, VM1.GND, J1.gnd, J2.gnd
  N7: Componente3.+, VM1.VCC
  N8: R2.pin_0, R3.pin_0, R4.pin_0, R10.pin_0

custom parts:
  Voltmeter (3 wire): Voltmeter, 3 digit LED (.56 inch) output, 3 wire (Power 3.5V to 30V, Ground, Vin) comes in several colors (red, green, orange, blue). Available from Ebay and Amazon and others, no bezel (although bezels to fit them are currently available on Ebay). The mounting ears on what you get may or may not be the same as the ones I have. Won't run on 3.3V so you would need a 5 volt source or a 3V to 5V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
